# Fritzing sketch Шаблон электросхемы проекта (2) kostya (saved by Fritzing 0.9.3b)
breadboards: 1

parts:
  Часть1 = Arduino Uno (Rev3)
  VCC1 = Battery
  S1 = Toggle Switch [package=THT]
  S2 = Pushbutton [package="[THT]"]
  S3 = Pushbutton [package="[THT]"]
  S4 = Pushbutton [package="[THT]"]
  Display1 = 4-Digit 7-segment LED Display [package=THT]
  SEN1 = Pulse Sensor [package=SIP]
  Q2 = NPN-Transistor [package="SOT-23 [SMD]"]
  R2 = Resistor [tolerance=±5% resistance=2.2k package=THT]

nets:
  N1: Часть1.D10_PWM/SS, Display1.DIO
  N2: Часть1.D12/MISO, Display1.CLK
  N3: Часть1.D2, S2.Pin_3, S2.Pin_4
  N4: Часть1.D3_PWM, S3.Pin_3, S3.Pin_4
  N5: Часть1.D4, S4.Pin_3, S4.Pin_4
  N6: Часть1.D5_PWM, Q2.0, R2.Pin_0
  N7: Часть1.D6_PWM, SEN1.Signal
  N8: Часть1.GND, S1.L2, S2.Pin_1, S2.Pin_2, S3.Pin_1, S3.Pin_2, S4.Pin_1, S4.Pin_2, Q2.2
  N9: Часть1.VIN, VCC1.+, R2.Pin_1
  N10: VCC1.-, S1.L1
  GND: Display1.GND, SEN1.GND
  VCC: Display1.VCC, SEN1.Vcc

custom parts:
  4-Digit 7-segment LED Display: A 4-digit 7-segments LED display PCB module driven by a TM1637 control IC via 1-wire protocol.
  Pulse Sensor: Pulse Sensor Optical Heart Rate Monitor for Arduino and other microcontrollers
